# Fritzing sketch spark-door-state-monitor (saved by Fritzing 0.9.1b)
breadboards: 1

parts:
  Part1 = Spark Core (v1.0)
  S1 = Reed switch [package=THT]

nets:
  N1: Part1.GND, S1.pin_2
  N2: Part1.D0, S1.pin_1
